# Fritzing sketch 3-Top 10 (saved by Fritzing 0.9.4)
circuit board: 6.55825cm x 9.31668cm
breadboards: 1

parts:
  PM25 = IC, SIP package, 4 pins [chip_label=IC]
  Part48 = Adafruit MLX90640 Thermal Camera [part_number="Adafruit #4407"]
  TSL2596 = Adafruit TSL2591 High Dynamic Range Digital Light Sensor [part_number="Adafruit #1980"]
  Part50 = Adafruit AS7341
  Part51 = Adafruit HTU21D-F Temperature & Humidity Sensor [part_number="Adafruit #1899"]
  Part53 = Adafruit BMP388 [part_number="Adafruit #3966"]
  Sensor6 = Wind Sensor rev C4 [part_number=MD0550]
  Part54 = Adafruit MAX9814 Electret Microphone Amplifier [part_number="Adafruit #1713"]
  Part55 = Adafruit BNO055 STEMMA QT [part_number="Adafruit #4646"]
  Part56 = I2C level shifter bidirectional
  PWR = IC, SIP package, 3 pins [chip_label=IC]
  FET8 = STP16NF06 N-Channel Power MOSFET
  FET10 = STP16NF06 N-Channel Power MOSFET
  I2C = male pin header, 2 pins [form="♂ (male)"]
  ANALOG = male pin header, 2 pins [form="♂ (male)"]
  R2 = Resistor [tolerance=±5% resistance=220 package=THT]
  Part52 = Adafruit SGP30 [part_number="Adafruit #3709"]
  PM28 = Adafruit PMSA003I Air Quality Breakout [part_number="Adafruit #4632"]  # not connected
  MOSFET = male pin header, 2 pins [form="♂ (male)"]
  Part49 = Adafruit LTR390 UV Light Sensor [part_number="Adafruit #4831"]

nets:
  GND: PM25.pin1, Part48.GND, TSL2596.GND, Part50.GND, Part51.GND, Part53.GND, Sensor6.GND, Part54.GND, Part55.GND, Part56.GND, PWR.pin1, Part52.GND, Part49.GND
  N1: PM25.pin2, Part48.SCL, Part50.SCL, Part51.SCL, Part53.SCK/SCL, Part55.SCL, FET8.source, I2C.pin2, Part52.SCL, Part49.SCL
  N2: PM25.pin3, Part48.SDA, TSL2596.SDA, Part50.SDA, Part51.SDA, Part53.SDI/SDA, Part55.SDA, I2C.pin1, Part52.SDA, Part49.SDA
  N3: PM25.pin4, FET10.source
  VCC: Part48.VCC, TSL2596.VCC, Part50.VCC, Part51.VCC, Part53.VCC, Part55.VCC, Part56.LV, PWR.pin2, Part52.VCC, Part49.VCC
  N4: TSL2596.SCL, FET8.drain
  N5: Sensor6.+V, Part54.VDD, Part56.HV, PWR.pin3, FET10.drain
  N6: Sensor6.Out, R2.Pin_0
  N7: Part54.OUTPUT, Part56.HV4
  N8: Part56.LV4, ANALOG.pin2
  N9: Part56.LV3, ANALOG.pin1
  N10: Part56.LV2, MOSFET.pin2
  N11: Part56.LV1, MOSFET.pin1
  N12: Part56.HV1, FET8.gate
  N13: Part56.HV2, FET10.gate
  N14: Part56.HV3, R2.Pin_1

notes:
  SDA
  5V
  SCL
  VCC
  GND
  TSL
  PM25
  WND
  MIC
  Tricorder V1
  Shivam Kundan

custom parts:
  Adafruit MLX90640 Thermal Camera: You can now add affordable heat-vision to your project and with an Adafruit MLX90640 Thermal Camera Breakout. This sensor contains a 24x32 array of IR thermal sensors. When connected to your microcontroller (or Raspberry Pi) it will return an array of 768 individual infrared temperature readings over I2C. It's like those fancy thermal cameras, but compact and simple enough for easy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
  Adafruit TSL2591 High Dynamic Range Digital Light Sensor: When the future is dazzlingly-bright, this ultra-high-range luminosity sensor will help you measure it. The TSL2591 luminosity sensor is an advanced digital light sensor, ideal for use in a wide range of light situations. Compared to low cost CdS cells, this sensor is more precise, allowing for exact lux calculations and can be configured for different gain/timing ranges to detect light ranges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
  Adafruit HTU21D-F Temperature & Humidity Sensor: It's summer and you're sweating and your hair's all frizzy and all you really want to know is why the weatherman said this morning that today's relative humidity would max out at a perfectly reasonable 52% when it feels more like 77%. Enter the HTU21D-F Temperature + Humidity Sensor - the best way to prove the weatherman wrong! This I2C digital humidity sensor is an accurate and intelligent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
  Adafruit BMP388: Bosch has been a leader in barometric pressure sensors, from the BMP085. BMP180, and BMP280... now we've got the next generation, the Adafruit BMP388 Precision Barometric Pressure sensor. As you would expect, this sensor is similar to its earlier versions but even better. The BMP388 has better precision than ever, which makes it excellent for environmental sensing or as a precision altimeter.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
  Wind Sensor rev C4: Modern Device Thermal Anemometer rev. C4
  Adafruit MAX9814 Electret Microphone Amplifier: Add an ear to your project with this well-designed electret microphone amplifier with AGC. This fully assembled and tested board comes with a 20-20KHz electret microphone soldered on. For the amplification, we use the Maxim MAX9814, a specialty chip that is designed for amplifying electret microphones in situations where the loudness of the audio isn't predictable. This fancy microphone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
  Adafruit BNO055 STEMMA QT: If you've ever ordered and wire up a 9-DOF sensor, chances are you've also realized the challenge of turning the sensor data from an accelerometer, gyroscope, and magnetometer into actual "3D space orientation"! Orientation is a hard problem to solve. The sensor fusion algorithms (the secret sauce that blends accelerometer, magnetometer, and gyroscope data into stable three-axis orientation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
  I2C level shifter bidirectional: This is an interface board to connect 5V I2C to 3V I2C. It is bidirectinal.
  STP16NF06 N-Channel Power MOSFET: STP16NF06 N-channel Power MOSFET
  Adafruit SGP30: Breathe easy with the SGP30 Multi-Pixel Gas Sensor, a fully integrated MOX gas sensor. This is a very fine air quality sensor from the sensor experts at Sensirion, with I2C interfacing and fully calibrated output signals with a typical accuracy of 15% within measured values. The SGP combines multiple metal-oxide sensing elements on one chip to provide more detailed air quality signals. This is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
  Adafruit PMSA003I Air Quality Breakout: Breathe easy, knowing that you can track and sense the quality of the air around you with this Adafruit PMSA003I Air Quality Breakout. This sensor is great for monitoring air quality, in a compact plug-in format. Best of all, unlike almost all other sensors we've seen that are UART interface, this one is I2C interface, which makes it a great match for single board Linux computers like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
  Adafruit LTR390 UV Light Sensor: The LTR390 is one of the few low-cost UV sensors available, and it's a pretty nice one! With both ambient light and UVA sensing with a peak spectral response between 300 and 350nm. You can use it for measuring how much sun you can get before needing to covering up. Unlike the Si1145, this sensor will not give you UV Index readings. However, the Si1145 does UV Index approximations based on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
