# Fritzing sketch Bottom (saved by Fritzing 0.9.4)
circuit board: 12.16cm x 10.76cm
breadboards: 1

parts:
  J8 = Lidar2 [form="♀ (female)" package=THT]  # not connected
  MOSFET = male pin header, 2 pins [form="♂ (male)"]
  Geieger = male pin header, 2 pins [form="♂ (male)"]
  GPS = male pin header, 3 pins [form="♂ (male)"]
  ANALOG = male pin header, 2 pins [form="♂ (male)"]
  I2C = male pin header, 2 pins [form="♂ (male)"]
  PWR = IC, SIP package, 3 pins [chip_label=IC]
  Part1 = Adafruit ESP32 Feather V2
  Part2 = Adafruit LC709203F Fuel Gauge and Battery Monitor [part_number="Adafruit #4712"]
  Part3 = INA 260
  Part4 = PowerBoost 1000 Basic
  Part5 = NeoPixel Stick [part_number=1426]
  OLED_L = OLED 128x64 I2C Monochrome Display
  OLED_R = OLED 128x64 I2C Monochrome Display
  Part6 = Adafruit TCA4307 [part_number="Adafruit #5159"]
  Part7 = Adafruit LTC4311 I2C Extender
  Pad1 = Pad [width=3.4995555555555717 height=1.4534444444444443 connect=center]
  Pad2 = Pad [width=3.4807407407407513 height=1.5992592592592605 connect=center]
  Pad3 = Pad [width=3.4995555555555717 height=1.4534444444444443 connect=center]
  BATT = SPST Switch [package=switch-spdt]
  VIN+ = SPST Switch [package=switch-spdt]
  VIN- = SPST Switch [package=switch-spdt]
  FSR = female pin header, 2 pins [form="♀ (female)"]
  Pad4 = Pad [width=7.356215705115577 height=7.36 connect=center]
  Pad5 = Pad [width=7.356215705115577 height=7.36 connect=center]
  Pad6 = Pad [width=7.356215705115577 height=7.36 connect=center]
  Pad7 = Pad [width=7.356215705115577 height=7.36 connect=center]
  1KΩ = Resistor [tolerance=±5% resistance=220 package=THT]
  LiDAR = SPST Switch [package=switch-spdt]
  FSR_2 = SIP - 2 pins [chip_label=IC package="SIP (Single Inline) [THT]"]  # not connected
  LiDAR_2 = male pin header, 3 pins [form="♂ (male)"]
  VCC = female pin header, 1 pin [form="♀ (female)"]
  J9 = female pin header, 1 pin [form="♀ (female)"]
  Pad9 = Pad [width=1.693323925925931 height=1.2229723703703699 connect=center]
  Pad8 = Pad [width=1.693323925925931 height=1.2229723703703699 connect=center]
  RST! = SPST Switch [package=switch-spdt]

nets:
  N1: MOSFET.pin1, Part1.A1
  N2: MOSFET.pin2, Part1.IO32
  N3: Geieger.pin1, Part1.A0
  N4: Geieger.pin2, Part1.I37
  N5: GPS.pin1, Part1.IO14
  N6: GPS.pin2, Part1.IO8
  N7: GPS.pin3, Part1.RX
  N8: ANALOG.pin1, Part1.A2
  N9: ANALOG.pin2, Part1.A3
  N10: I2C.pin1, Part2.SDA, Part3.SDA, OLED_L.SDA, OLED_R.SDA, Part6.SDA_OUT
  N11: I2C.pin2, Part2.SCL, Part3.SCL, OLED_L.SCK, OLED_R.SCK, Part6.SCL_OUT
  GND: PWR.pin1, Part1.GND, Part2.GND, Part3.GND, Part4.GND, Part5.GND, OLED_L.GND, OLED_R.GND, Part6.GND, Part7.GND, Pad1.pad, LiDAR_2.pin2, RST!.O
  VCC: PWR.pin2, Part2.VCC, Part3.VCC, OLED_L.VDD, OLED_R.VDD, Part6.VCC, Part7.VCC, VCC.pin1, Pad8.pad
  N12: PWR.pin3, Part4.5.0V, Part5.+5V, Pad2.pad, FSR.pin1, LiDAR.O
  N13: Part1.MISO, J9.pin1
  N14: Part1.MOSI, 1KΩ.Pin_1
  N15: Part1.SCK, 1KΩ.Pin_0, LiDAR_2.pin3
  N16: Part1.A5, Part5.DATAIN, Pad3.pad
  N17: Part1.A4, FSR.pin2
  N18: Part1.3.3V, Pad9.pad
  N19: Part1.!RESET, RST!.P
  N20: Part1.VBAT, VIN+.S, VIN-.O
  N21: Part1.IO13, Part4.ENABLE
  N22: Part1.IO12, Pad7.pad
  N23: Part1.IO27, Pad6.pad
  N24: Part1.IO33, Pad5.pad
  N25: Part1.IO15, Pad4.pad
  N26: Part1.SCL, Part6.SCL_IN, Part7.SCL
  N27: Part1.SDA, Part6.SDA_IN, Part7.SDA
  N28: Part2.VBAT, BATT.O
  N29: Part3.IN+, VIN+.O
  N30: Part3.IN-, VIN-.P
  N31: BATT.P, VIN+.P
  N32: LiDAR.P, LiDAR_2.pin1

notes:
  PWR
  RX
  TX
  VCC
  5V
  SDA
  SCL
  GND
  TSL
  PM25
  WND
  MIC
  OFF
  ON
  +
  -
  SIG

custom parts:
  Lidar2: Generic female header
  Adafruit LC709203F Fuel Gauge and Battery Monitor: Low cost Lithium Polymer batteries have revolutionized electronics - they're thin, they're light, they can be regulated down to 3.3V and they're easy to charge. On your phone, there's a little image of a battery cell that tells you the percentage of charge - so you know when you absolutely need to plug it in and when you can stay untethered. The Adafruit LC709203F LiPoly / LiIon Fuel Gauge and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
  INA 260: Rev. B, add copy
  PowerBoost 1000 Basic: The PowerBoost 1000 is a little DC/DC boost converter module that can run from 1.8V batteries or higher, and convert the battery output to 5.2V DC for running your 5V projects. At its heart is a TPS61030 boost converter from TI. This boost converter chip has some really nice extras such as low battery detection, 4A internal switch, synchronous conversion, excellent efficiency, and 700KHz high-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
  NeoPixel Stick: Make your own little LED strip arrangement with this stick of NeoPixel LEDs. We crammed 8 of the tiny 5050 (5mm x 5mm) smart RGB LEDs onto a PCB with mounting holes and a chainable design. Use only one microcontroller pin to control as many as you can chain together! Each LED is addressable as the driver chip is inside the LED. Each one has ~18mA constant current drive so the color will be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
  Adafruit TCA4307: As we've been adding STEMMA QT connectors to our breakouts and dev boards, folks have been really enjoying the simplicity and speed of plugging in I2C sensors and devices for quick iteration and design. That's all good, but I2C wasn't really designed for hot-plugging. You're kinda supposed to have everything connected once on boot and never mess with it - I2C was specified for on-board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
  SIP - 2 pins: A SIP stand-in part for whatever you want. With 2 pins on a 300 mil single inline package (SIP) footprint.
