# Fritzing sketch Mid 4 (saved by Fritzing 0.9.4)
circuit board: 12.16cm x 10.76cm
breadboards: 1

parts:
  MOSFET = male pin header, 2 pins [form="♂ (male)"]  # not connected
  ANALOG = male pin header, 2 pins [form="♂ (male)"]  # not connected
  I2C = male pin header, 2 pins [form="♂ (male)"]  # not connected
  PWR = IC, SIP package, 3 pins [chip_label=IC]
  J1 = Geiger Module [form="♂ (male)" package=THT]  # not connected
  GPS = BN880 GPS [package="SIP (Single Inline) [THT]"]  # not connected
  Part1 = I2C level shifter bidirectional
  GPS_2 = male pin header, 3 pins [form="♂ (male)"]
  Geiegr = male pin header, 2 pins [form="♂ (male)"]
  Geiger = male pin header, 3 pins [form="♂ (male)"]
  FET9 = STP16NF06 N-Channel Power MOSFET
  FET10 = STP16NF06 N-Channel Power MOSFET
  J4 = Generic female header - 2 pins [form="♀ (female)" package=THT]
  GPS_3 = male pin header, 4 pins [form="♂ (male)"]
  Piezo_PWR = male pin header, 2 pins [form="♂ (male)"]
  IR_LED_PWR = SWITCH_SPDT [package=kps-1290]
  J2 = IR Cut Camera [form="♀ (female)" package=THT]  # not connected
  PIEZO = SPST Switch [package=switch-spdt]

nets:
  N1: PWR.pin1, Part1.GND, Geiger.pin2, J4.pin2, GPS_3.pin4
  N2: PWR.pin2, Part1.LV, IR_LED_PWR.O
  N3: PWR.pin3, Part1.HV, FET9.drain, FET10.drain
  N4: Part1.LV4, Geiegr.pin1
  N5: Part1.LV1, GPS_2.pin1
  N6: Part1.HV1, FET10.gate
  N7: Part1.HV4, FET9.gate
  N8: GPS_2.pin2, GPS_3.pin2
  N9: GPS_2.pin3, GPS_3.pin3
  N10: Geiegr.pin2, Geiger.pin3
  N11: Geiger.pin1, FET9.source
  N12: FET10.source, GPS_3.pin1
  N13: J4.pin1, IR_LED_PWR.P
  N14: Piezo_PWR.pin1, PIEZO.S
  N15: Piezo_PWR.pin2, PIEZO.P

notes:
  GND
  VCC
  SCL
  5V
  SDA
  MIC
  WND
  TSL
  PM25
  RX
  TX
  ON
  OFF
  +
  -
  D
  PWR
  Ode to Spot
  - Lt. Cmdr. Data
  3.3V

custom parts:
  BN880 GPS: A SIP stand-in part for whatever you want. With 6 pins on a 300 mil single inline package (SIP) footprint.
  I2C level shifter bidirectional: This is an interface board to connect 5V I2C to 3V I2C. It is bidirectinal.
  STP16NF06 N-Channel Power MOSFET: STP16NF06 N-channel Power MOSFET
  Generic female header - 2 pins: Generic female header
  SWITCH_SPDT: Side-actuated SPDT slide switch, as used on the Arduino Pro
