# Fritzing sketch pi4_hyperpixel (saved by Fritzing 0.9.4)
circuit board: 12.16cm x 10.76cm
breadboards: 1

parts:
  raspberry_pi_40_pin_header1 = raspberry pi 40 pin header [part_number=RPI-3-V1.2]
  Raspberry_Pi_3_Blank1 = Raspberry Pi 3 Blank [part_number=RPI-3-V1.2]  # not connected
  Hyperpixel1 = Hyperpixel [part_number=RPI-3-V1.2]
  PWR = SPST Switch [package=switch-spdt]
  J1 = female pin header, 2 pins [form="♀ (female)"]

nets:
  3V3: raspberry_pi_40_pin_header1.3v3, raspberry_pi_40_pin_header1.3V3, Hyperpixel1.3v3, Hyperpixel1.3V3
  N1: raspberry_pi_40_pin_header1.GPIO2, Hyperpixel1.GPIO2
  N2: raspberry_pi_40_pin_header1.GPIO3, Hyperpixel1.GPIO3
  N3: raspberry_pi_40_pin_header1.GPIO4, Hyperpixel1.GPIO4
  GND: raspberry_pi_40_pin_header1.GND, Hyperpixel1.GND, J1.pin1
  N4: raspberry_pi_40_pin_header1.GPIO17, Hyperpixel1.GPIO17
  N5: raspberry_pi_40_pin_header1.GPIO27, Hyperpixel1.GPIO27
  N6: raspberry_pi_40_pin_header1.GPIO22, Hyperpixel1.GPIO22
  N7: raspberry_pi_40_pin_header1.GPIO10, Hyperpixel1.GPIO10
  N8: raspberry_pi_40_pin_header1.GPIO9, Hyperpixel1.GPIO9
  N9: raspberry_pi_40_pin_header1.GPIO11, Hyperpixel1.GPIO11
  N10: raspberry_pi_40_pin_header1.ID_SD, Hyperpixel1.ID_SD
  N11: raspberry_pi_40_pin_header1.GPIO5, Hyperpixel1.GPIO5
  N12: raspberry_pi_40_pin_header1.GPIO6, Hyperpixel1.GPIO6
  N13: raspberry_pi_40_pin_header1.GPIO13, Hyperpixel1.GPIO13
  N14: raspberry_pi_40_pin_header1.GPIO19, Hyperpixel1.GPIO19
  N15: raspberry_pi_40_pin_header1.GPIO26, Hyperpixel1.GPIO26
  N16: raspberry_pi_40_pin_header1.GPIO21, Hyperpixel1.GPIO21
  N17: raspberry_pi_40_pin_header1.GPIO20, Hyperpixel1.GPIO20
  N18: raspberry_pi_40_pin_header1.GPIO16, Hyperpixel1.GPIO16
  N19: raspberry_pi_40_pin_header1.GPIO12, Hyperpixel1.GPIO12
  N20: raspberry_pi_40_pin_header1.ID_SC, Hyperpixel1.ID_SC
  N21: raspberry_pi_40_pin_header1.GPIO7, Hyperpixel1.GPIO7
  N22: raspberry_pi_40_pin_header1.GPIO8, Hyperpixel1.GPIO8
  N23: raspberry_pi_40_pin_header1.GPIO25, Hyperpixel1.GPIO25
  N24: raspberry_pi_40_pin_header1.GPIO24, Hyperpixel1.GPIO24
  N25: raspberry_pi_40_pin_header1.GPIO23, Hyperpixel1.GPIO23
  N26: raspberry_pi_40_pin_header1.GPIO18, Hyperpixel1.GPIO18
  N27: raspberry_pi_40_pin_header1.GPIO15, Hyperpixel1.GPIO15
  N28: raspberry_pi_40_pin_header1.GPIO14, Hyperpixel1.GPIO14
  5V: raspberry_pi_40_pin_header1.5V, Hyperpixel1.5V, PWR.P
  N29: PWR.S, J1.pin2

notes:
  GND
  5V

custom parts:
  raspberry pi 40 pin header: The RPi3, a faster version of the awesome Raspberry Pi 2 B ARM Board with 40 pin gpio. Ready for special Raspberry Pi B+ and RPi2 Hat (Hardware attached (on) top)
  Raspberry Pi 3 Blank: The RPi3, a faster version of the awesome Raspberry Pi 2 B ARM Board with 40 pin gpio. Ready for special Raspberry Pi B+ and RPi2 Hat (Hardware attached (on) top)
